# Fritzing sketch calibrate (saved by Fritzing 0.8.7b)
breadboards: 1

parts:
  Part1 = Arduino Uno (Rev3)
  J2 = Basic Servo

nets:
  N1: Part1.D9_PWM, J2.pulse
  5V: Part1.5V, J2.vcc
  GND: Part1.GND, J2.gnd
