# Fritzing sketch light-combination (saved by Fritzing 0.8.7b)
breadboards: 1

parts:
  Part1 = Arduino Uno (Rev3)
  J1 = Basic Servo
  R1 = Rotary Potentiometer (Small) [maximum_resistance=100kΩ package=THT]
  LED2 = LED - 5mm [color="Yellow (585nm)" package="5 mm [THT]"]
  LED3 = LED - 5mm [color="Red (633nm)" package="5 mm [THT]"]
  R3 = Resistor [tolerance=±5% resistance=220 package=THT]
  R4 = Resistor [tolerance=±5% resistance=220 package=THT]
  R5 = Resistor [tolerance=±5% resistance=220 package=THT]
  LED1 = smd LED [color="Green (555nm)" package="1206 [SMD]"]

nets:
  N1: Part1.A0, R1.wiper
  N2: Part1.D9_PWM, J1.pulse
  N3: Part1.D3_PWM, R3.Pin_0
  N4: Part1.D4, R4.Pin_0
  N5: Part1.D5_PWM, R5.Pin_0
  5V: Part1.5V, J1.vcc, R1.leg2
  GND: Part1.GND, J1.gnd, R1.leg1, LED2.cathode, LED3.cathode, LED1.cathode
  N6: LED2.anode, R4.Pin_1
  N7: LED3.anode, R5.Pin_1
  N8: R3.Pin_1, LED1.anode
