# Fritzing sketch one-button (saved by Fritzing 0.8.7b)
breadboards: 1

parts:
  Part1 = Arduino Uno (Rev3)
  J1 = Basic Servo
  S3 = Pushbutton [package="[THT]"]

nets:
  N1: Part1.D9_PWM, J1.pulse
  N2: Part1.D10_PWM/SS, S3.Pin_3, S3.Pin_4
  5V: Part1.5V, J1.vcc
  GND: Part1.GND, J1.gnd, S3.Pin_1, S3.Pin_2
